# Fritzing sketch blink_schematics (saved by Fritzing 0.9.3b)
breadboards: 1

parts:
  Raspberry_Pi_1 = Raspberry Pi 3 [part_number=RPI-3-V1.2]
  R2 = Resistor [tolerance=±1% resistance=1k package=THT]
  LED1 = LED - 3mm [color="Red (633nm)" package="3 mm [THT]"]
  LED2 = LED - 3mm [color="Blue (430nm)" package="3 mm [THT]"]
  R3 = Resistor [tolerance=±1% resistance=1k package=THT]
  J1 = Piezo Speaker
  S1 = Pushbutton [package="[THT]"]
  R4 = Resistor [tolerance=±5% resistance=220 package=THT]

nets:
  N1: Raspberry_Pi_1.GND, LED1.cathode, LED2.cathode, J1.pin1, S1.Pin_1, S1.Pin_2
  N2: Raspberry_Pi_1.GPIO5, R2.Pin_0
  N3: Raspberry_Pi_1.GPIO6, R3.Pin_1
  N4: Raspberry_Pi_1.GPIO13, J1.pin2
  N5: Raspberry_Pi_1.GPIO21, S1.Pin_3, S1.Pin_4, R4.Pin_1
  N6: Raspberry_Pi_1.5V, R4.Pin_0
  N7: R2.Pin_1, LED2.anode
  N8: LED1.anode, R3.Pin_0

notes:
  Sysolve IoT开源项目
  Android Things Simple PIO 扩展案例 - 报警器
  购买所需元件？请访问sysolve.taobao.com
